# Fritzing sketch Untitled Sketch (saved by Fritzing 0.9.3b)
breadboards: 2

parts:
  HC-SR04_Sensor_1 = HC-SR04 Ultrasonic Distance Sensor
  Capacitive_Soil_Moisture_Sensor1 = DFRobot Capacitive Soil Moisture Sensor V1.0 [part_number=SEN0193]
  VCC1 = Battery block 9V
  Mod3 = Raspberry Pi Pico W
  Capacitive_Soil_Moisture_Sensor2 = DFRobot Capacitive Soil Moisture Sensor V1.0 [part_number=SEN0193]
  Capacitive_Soil_Moisture_Sensor3 = DFRobot Capacitive Soil Moisture Sensor V1.0 [part_number=SEN0193]
  Mod4 = KY-019 5V Relay Module [package="Breakout board"]
  Mod5 = KY-019 5V Relay Module [package="Breakout board"]
  Mod6 = KY-019 5V Relay Module [package="Breakout board"]
  Part1 = submersible pump
  Part2 = submersible pump
  Part3 = submersible pump

nets:
  N1: HC-SR04_Sensor_1.VCC, VCC1.+, Mod4.+, Mod4.Common, Mod5.+, Mod5.Common, Mod6.+, Mod6.Common
  N2: HC-SR04_Sensor_1.TRIG, Mod3.pin_1
  N3: HC-SR04_Sensor_1.ECHO, Mod3.pin_2
  GND: HC-SR04_Sensor_1.GND, Capacitive_Soil_Moisture_Sensor1.GND, Mod3.pin_3, Mod3.pin_8, Mod3.pin_13, Mod3.pin_18, Mod3.pin_23, Mod3.pin_28, Mod3.pin_33, Mod3.pin_38, Capacitive_Soil_Moisture_Sensor2.GND, Capacitive_Soil_Moisture_Sensor3.GND
  N4: Capacitive_Soil_Moisture_Sensor1.A, Mod3.pin_31
  VCC: Capacitive_Soil_Moisture_Sensor1.VCC, Mod3.pin_36, Capacitive_Soil_Moisture_Sensor2.VCC, Capacitive_Soil_Moisture_Sensor3.VCC
  N5: VCC1.-, Mod4.-, Mod5.-, Mod6.-, Part1.pin1, Part2.pin1, Part3.pin1
  N6: Mod3.pin_17, Mod4.S
  N7: Mod3.pin_19, Mod6.S
  N8: Mod3.pin_20, Mod5.S
  N9: Mod3.pin_32, Capacitive_Soil_Moisture_Sensor3.A
  N10: Mod3.pin_34, Capacitive_Soil_Moisture_Sensor2.A
  N11: Mod4.NO, Part1.pin2
  N12: Mod5.NO, Part3.pin2
  N13: Mod6.NO, Part2.pin2

custom parts:
  DFRobot Capacitive Soil Moisture Sensor V1.0: DFRobot Capacitive Soil Moisture Sensor V1.0 This product measures soil moisture levels by capacitive sensing, rather than resistive sensing like other types of moisture sensor. It is made of a corrosion resistant material giving it a long service life. Insert it into soil and impress your friends with the real-time soil moisture data! The product includes an on-board voltage regulator which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
  Raspberry Pi Pico W: Raspberry Pi Pico W. Based around the RP2040 microcontroller the Pico W is a low cost microcontroller device bringing Raspberry Pi quality, cost, and easy of use to the microcontroller space. The areas marked KEEPOUT in pcb silkscreen should not have traces running through them to avoid shorts on a soldered in module!
  KY-019 5V Relay Module: KY-019 5V Relay module, used to control AC circuits. (Special thanks to vanepp for fixing the PCB holes and other errors)
  submersible pump: pump
